# Fritzing sketch conexoes_cyberPlanta (saved by Fritzing 0.9.2b)
breadboards: 1

parts:
  U1 = NodeMCU V1.0
  부품3 = FC-28 Soil Hygrometer Module - Probe
  부품4 = FC-28 Soil Hygrometer Module
  DHT1 = DHT11 Humitidy and Temperature Sensor
  Componente1 = BH1750
  R1 = Resistor [tolerance=±5% resistance=220 package=THT]
  M1 = DC Motor
  KY-1 = Keyes Relay [package=THT]

nets:
  N1: U1.D1, Componente1.SCL
  N2: U1.D2, Componente1.SDA
  N3: U1.D4, KY-1.signal
  VCC: U1.3V3, 부품4.VCC, DHT1.VDD, Componente1.VCC, KY-1.power
  GND: U1.GND, 부품4.GND, DHT1.GND, Componente1.GND, R1.Pin_0, KY-1.ground
  N4: U1.D5, DHT1.DATA, R1.Pin_1
  N5: U1.A0, 부품4.AO
  N6: 부품3.POS, 부품4.POS
  N7: 부품3.NEG, 부품4.NEG
  N8: M1.pin_1, KY-1.C
  N9: M1.pin_2, KY-1.NO

notes:
  Bomba Hidraulica

custom parts:
  NodeMCU V1.0: ESP8266 based NodeMCU
  FC-28 Soil Hygrometer Module - Probe: The FC-28 is a soil hygrometer module that uses the Texas Instruments LM393 comparator chip to provide an analog measurement of soil humidity.
  FC-28 Soil Hygrometer Module: The FC-28 is a soil hygrometer module that uses the Texas Instruments LM393 comparator chip to provide an analog measurement of soil humidity. The digital output is high when soil moisture is over a certain threshold, as determined by adjusting the potentiometer.
  DHT11 Humitidy and Temperature Sensor: DHT11 Humidity and Temperature Sensor
  BH1750: Light Sensor
  Keyes Relay: The Keyes 5V relay module is suitable for SCM development, home appliance control. It uses a 5V~12V TIL control signal which can control DC / AC signal.
